# Fritzing sketch Button_LED (saved by Fritzing 0.9.3b)
breadboards: 1

parts:
  Raspberry_Pi1 = Raspberry Pi B+
  S3 = Pushbutton [package="[SMD]"]
  R1 = Resistor [tolerance=±5% resistance=10k package="1206 [SMD]"]
  R2 = Resistor [tolerance=±5% resistance=220 package="2010 [SMD]"]
  LED1 = LED - 5mm [color="Red (633nm)" package="5 mm [THT]"]

nets:
  N1: Raspberry_Pi1.3v3, R1.Pin_1
  N2: Raspberry_Pi1.GPIO13, S3.Pin_1, S3.Pin_2, R1.Pin_0
  N3: Raspberry_Pi1.GND, S3.Pin_3, S3.Pin_4, R2.Pin_0
  N4: Raspberry_Pi1.GPIO12, LED1.anode
  N5: R2.Pin_1, LED1.cathode

notes:
  3.3V
  GPIO 13
  GPIO 12
