# Fritzing sketch Nano_Yes_No (saved by Fritzing 0.9.3b)
breadboards: 1

parts:
  Part1 = Arduino Nano 33 BLE Sense [part_number="Nano 33 Sense"]
  LED1 = LED - 5mm [color="Green (555nm)" package="5 mm [THT]"]
  R1 = Resistor [tolerance=±5% resistance=220 package=THT]
  R2 = Resistor [tolerance=±5% resistance=220 package=THT]
  LED2 = LED - 5mm [color="Red (633nm)" package="5 mm [THT]"]

nets:
  N1: Part1.GND, Part1.A7, R1.Pin_1, R2.Pin_1
  N2: Part1.D2, LED1.anode
  N3: Part1.D4, LED2.anode
  N4: Part1.D11/MOSI, Part1.+5V
  N5: LED1.cathode, R1.Pin_0
  N6: R2.Pin_0, LED2.cathode

notes:
  RPi GPIO 13
  RPi GND

custom parts:
  Arduino Nano 33 BLE Sense: The Nano 33 BLE Sense (without headers) is Arduino’s 3.3V AI enabled board in the smallest available form factor: 45x18mm! The Arduino Nano 33 BLE Sense is a completely new board on a well-known form factor. It comes with a series of embedded sensors: 9 axis inertial sensor: what makes this board ideal for wearable devices humidity, and temperature sensor: to get highly accurate measurements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
